# Fritzing sketch circuit wiring (saved by Fritzing 0.9.3b)
breadboards: 3

parts:
  Tiva_C_LaunchPad1 = Tiva C TM4C123G [package=THT]
  Part1 = Arduino Uno (Rev3) - ICSP
  Mod1 = KY-024 Linear Hall Magnetic Sensor Module [package="Breakout board"]
  HC-SR04_Sensor_1 = HC-SR04 Ultrasonic Distance Sensor
  Part2 = Bluetooth HC-05 Macho
  1 = Piezo Speaker
  IC1 = MQ-2 [package="DIP (Dual Inline) [THT]"]
  Part3 = LCD1602-I2C
  LED1 = smd LED [color="Red (633nm)" package="0603 [SMD]"]
  J2 = Piezo Speaker
  LED3 = smd LED [color="Red (633nm)" package="0603 [SMD]"]
  S1 = Pushbutton [package="[THT]"]
  Mod2 = KY-022 Infrared Receiver Module [package="Breakout board"]
  LED4 = LED - 5mm [color="White (4500K)" package="5 mm [THT]"]

nets:
  N1: Tiva_C_LaunchPad1.PB0, HC-SR04_Sensor_1.ECHO
  N2: Tiva_C_LaunchPad1.PB1, Tiva_C_LaunchPad1.PD1, HC-SR04_Sensor_1.TRIG
  N3: Tiva_C_LaunchPad1.PE4, Part2.TXD
  N4: Tiva_C_LaunchPad1.PE5, Part2.RXD
  N5: Tiva_C_LaunchPad1.PD0, Mod1.D0
  N6: Tiva_C_LaunchPad1.PE2, Mod2.S
  N7: Tiva_C_LaunchPad1.PE3, IC1.pin4
  VCC: Tiva_C_LaunchPad1.PD6, Part1.5V, Mod1.+, HC-SR04_Sensor_1.VCC, Part2.VCC, IC1.pin1, Part3.VCC, S1.Pin_1, S1.Pin_2
  N8: Tiva_C_LaunchPad1.PD7, LED1.anode, J2.pin2
  N9: Tiva_C_LaunchPad1.PF3, 1.pin2, LED3.anode
  N10: Part1.A4/SDA, Part3.SCL
  N11: Part1.A5/SCL, Part3.SDA
  GND: Part1.GND, Mod1.G, HC-SR04_Sensor_1.GND, Part2.GND, 1.pin1, IC1.pin2, Part3.GND, LED1.cathode, J2.pin1, LED3.cathode, S1.Pin_3, S1.Pin_4, Mod2.-, LED4.cathode
  N12: Mod2.Vin, LED4.anode

custom parts:
  Tiva C TM4C123G: Tiva C LaunchPad EK-TM4C123GXL
  KY-024 Linear Hall Magnetic Sensor Module: KY-024 Linear Hall Magnetic Sensor Module reacts iin the presence of a magnetic field.
  MQ-2: MQ-2 Gas Sensor module
  LCD1602-I2C: A standard character display, usually with 2x16 characters. Comes in many colors with LCM1602 IIC attached.
  KY-022 Infrared Receiver Module: KY-022 IR receiver module, reacts to 38kHz infrared light.
